# Fritzing sketch UMC_PWR1310_0306 (saved by Fritzing 0.8.7b)
circuit board: 6.88566cm x 5.36311cm
breadboards: 1

parts:
  D010 = Diode [part_number=1N4148 package=diode-1n4148]
  D011 = Diode [part_number=1N4148 package=diode-1n4148]
  D012 = Diode [part_number=1N4148 package=diode-1n4148]
  C010 = Ceramic Capacitor [capacitance=100nF package="100 mil [THT, multilayer]"]
  C011 = Ceramic Capacitor [capacitance=100nF package="100 mil [THT, multilayer]"]
  D014 = Diode [part_number=1N4007 package=diode-1n4148]
  J051 = Header 3 [package=molex-1x3_lock]
  J032 = Header 3 [package=molex-1x3_lock]
  J031 = Header 3 [package=molex-1x3_lock]
  ACS712 = ACS712 Low Current Sensor Board v12
  X031 = screw terminal, 2 pins
  X032 = screw terminal, 2 pins
  D013 = Diode [part_number=1N4148 package=diode-1n4148]
  DEV-10182 = Monster Moto Shield
  IC010 = Voltage Regulator [package=to-220-alt]
  J061 = female pin header, 3 pins [form="♀ (female)"]
  J060 = female pin header, 3 pins [form="♀ (female)"]
  X011 = screw terminal, 2 pins
  X010 = screw terminal, 2 pins
  J011 = Header 3 [package=molex-1x3_lock]
  J050 = Header 3 [package=molex-1x3_lock]
  J010 = Header 4 [package=molex-1x4_lock]
  J052 = Header 4 [package=molex-1x4_lock]
  J053 = Header 4 [package=molex-1x4_lock]

nets:
  N1: D010.A, IC010.GND
  N2: D010.C, D011.A
  N3: D011.C, D012.A
  N4: D012.C, D013.A
  GND: C010.0, C011.1, J051.1, J032.1, J031.1, ACS712.GND, D013.C, DEV-10182.GND, DEV-10182.GND_-_GND@0, DEV-10182.GND_-_GND@1, DEV-10182.GND_-_GND@2, J061.pin1, J060.pin1, X011.pin1, X010.pin1, J011.1, J050.1, J010.1, J052.1, J053.1
  N5: C010.1, D014.C, ACS712.IP-, DEV-10182.VCC, IC010.IN
  7.2V: C011.0, D014.A, IC010.OUT, J061.pin2, J060.pin2, X011.pin2
  N6: J051.2, J031.3
  N7: J051.3, J032.3
  5.4V: J032.2, J031.2, ACS712.5V, DEV-10182.5V, J010.2
  010: ACS712.IP+, X010.pin2, J010.4
  N8: ACS712.VO, J010.3
  N9: X031.pin1, DEV-10182.OUTA1
  N10: X031.pin2, DEV-10182.OUTB1
  N11: X032.pin1, DEV-10182.OUTA2
  N12: X032.pin2, DEV-10182.OUTB2
  050A: DEV-10182.CS1_-_A2, J050.2
  050B: DEV-10182.CS2_-_A3, J050.3
  052B: DEV-10182.INA2_-_D4, J052.3
  051A: DEV-10182.PWM1_-_D5, J053.2
  052A: DEV-10182.PWM2_-_D6, J052.2
  051B: DEV-10182.INA1_-_D7, J053.3
  051C: DEV-10182.INB1_-_D8, J053.4
  052C: DEV-10182.INB2_-_D9, J052.4
  N13: J061.pin3, J011.3
  N14: J060.pin3, J011.2

notes:
  BATTERY
  AMC
  AME
  AMB
  MTB
  MTE
  AMT
  MEnSnI
  BlTSnI
  GND
  MEnAhd
  MEnAst
  MEnSpd
  BlTDvn
  BlTEmr
  BlTSpd
  BlTTmp
  MEnTmp
  AMS
  EngBtV
  5.4V
  EngBtI
  AMP
  7.2V
  U-BoatMC, U-Boat Module Controll - Power Shields, 0.306
  PWR
  +
  -
  SNR
  Current Sense
  RDT
  RDD
  RdrDpt
  RdrDir
  AMR
  M
  UMC_PWR1310 V0.306
  TPB
  TPE
