# Fritzing sketch UMC_131012_010 (saved by Fritzing 0.8.3b)
breadboards: 1

parts:
  Mega2560_Rev3 = Arduino Mega 2560 (Rev3)
  J530 = Header 4 [package=molex-1x4_lock]  # not connected
  J520 = Header 4 [package=molex-1x4_lock]  # not connected
  J510 = Header 4 [package=molex-1x4_lock]  # not connected
  J420 = Header 3 [package=molex-1x3_lock]
  J421 = Header 3 [package=molex-1x3_lock]
  J110 = Header 2 [package=jst-2-pth]
  J120 = Header 2 [package=jst-2-pth]
  Q130 = TRANSISTOR_NPN [package=to-92]
  Q140 = TRANSISTOR_NPN [package=to-92]
  Shield_ETH = Arduino Ethernet Shield (Rev3)  # not connected
  Q120 = TRANSISTOR_NPN [package=to-92]
  Q110 = TRANSISTOR_NPN [package=to-92]
  IC100 = Voltage Regulator [package=to-92]
  D101 = Diode [package=diode-1n4148]
  D102 = Diode [package=diode-1n4148]
  R111 = Resistor [tolerance=±5% resistance=220 package=THT]
  R121 = Resistor [tolerance=±5% resistance=220 package=THT]
  R110 = Resistor [tolerance=±5% resistance=220 package=THT]
  R120 = Resistor [tolerance=±5% resistance=220 package=THT]
  RH680 = Humidity and Temperature Sensor RHT03
  D100 = Rectifier Diode [part_number=1N4007 package="300 mil [THT]"]
  R130 = Resistor [tolerance=±5% resistance=220 package=THT]
  R140 = Resistor [tolerance=±5% resistance=220 package=THT]
  J101 = Header 4 [package=molex-1x4_lock]
  R142 = Resistor [tolerance=±5% resistance=220 package=THT]
  R132 = Resistor [tolerance=±5% resistance=220 package=THT]
  C100 = Ceramic Capacitor [capacitance=100nF package="100 mil [THT, multilayer]"]
  C101 = Ceramic Capacitor [capacitance=100nF package="100 mil [THT, multilayer]"]
  J620 = Header 3 [package=molex-1x3_lock]
  J622 = Header 3 [package=molex-1x3_lock]
  J623 = Header 3 [package=molex-1x3_lock]
  J626 = Header 3 [package=molex-1x3_lock]
  Q650 = TRANSISTOR_NPN [package=to-92]
  Q655 = TRANSISTOR_NPN [package=to-92]
  R650 = Resistor [tolerance=±5% resistance=220 package=THT]
  R655 = Resistor [tolerance=±5% resistance=220 package=THT]
  J621 = Header 3 [package=molex-1x3_lock]
  RaspberryPi_Rev2 = Raspberry Pi rev2  # not connected
  J540 = Header 3 [package=molex-1x3_lock]
  J450 = Header 4 [package=molex-1x4_lock]
  J591 = Header 3 [package=molex-1x3_lock]
  J105 = Header 4 [package=jst-4-pth]
  J107 = Header 2 [package=molex-1x2_lock]
  R101 = Resistor [tolerance=±5% resistance=220 package=THT]
  R102 = Resistor [tolerance=±5% resistance=220 package=THT]
  R121_2 = Resistor [tolerance=±5% resistance=220 package=THT]
  R106 = Resistor [tolerance=±5% resistance=220 package=THT]
  R105 = Resistor [tolerance=±5% resistance=220 package=THT]
  R680 = Resistor [tolerance=±5% resistance=220 package=THT]
  J106 = Header 2 [package=jst-2-pth]
  J624 = Header 3 [package=molex-1x3_lock]
  J625 = Header 3 [package=molex-1x3_lock]
  J590 = Header 2 [package=molex-1x2_lock]
  DEV-10182 = Monster Moto Shield
  X010 = Screw terminal - 2 pins [package=THT]
  IC010 = Voltage Regulator [package=to-220-alt]
  ACS713 = ACS712 Low Current Sensor Board v12
  D010 = Diode [package=diode-1n4148]
  D011 = Diode [package=diode-1n4148]
  D012 = Diode [package=diode-1n4148]
  X011 = Screw terminal - 2 pins [package=THT]
  J601 = female pin header, 8 pins [form="♀ (female)"]  # not connected
  J602 = female pin header, 8 pins [form="♀ (female)"]  # not connected
  J610 = female pin header, 4 pins [form="♀ (female)"]
  J600 = female pin header, 8 pins [form="♀ (female)"]  # not connected
  CP108 = female pin header, 4 pins [form="♀ (female)"]
  X100 = screw terminal, 2 pins
  J650 = Header 2 [package=molex-1x2_lock]
  R651 = Resistor [tolerance=±5% resistance=220 package=THT]
  SG655 = Buzzer 12mm [package=buzzer-12mm-ns-kit]
  J050 = Header 4 [package=molex-1x4_lock]
  X031 = Screw terminal - 2 pins [package=THT]
  X032 = Screw terminal - 2 pins [package=THT]
  J011 = Header 4 [package=molex-1x4_lock]
  C010 = Ceramic Capacitor [capacitance=100nF package="100 mil [THT, multilayer]"]
  C011 = Ceramic Capacitor [capacitance=100nF package="100 mil [THT, multilayer]"]
  D013 = Diode [package=diode-1n4148]
  J051 = Header 4 [package=molex-1x4_lock]
  J052 = Header 4 [package=molex-1x4_lock]
  J452 = Header 4 [package=molex-1x4_lock]
  J451 = Header 4 [package=molex-1x4_lock]
  J053 = Header 3 [package=molex-1x3_lock]
  J453 = Header 3 [package=molex-1x3_lock]
  J032 = Header 3 [package=molex-1x3_lock]
  J031 = Header 3 [package=molex-1x3_lock]

nets:
  GND: Mega2560_Rev3.GND, J420.1, J421.1, Q130.E, Q140.E, Q120.E, Q110.E, D101.C, RH680.GND_2, J101.4, J620.2, J622.2, J623.2, J626.2, Q650.E, Q655.E, J621.2, J540.2, J450.1, J591.3, J105.1, J107.2, R102.Pin_1, R106.Pin_1, J106.2, J624.2, J625.2, DEV-10182.GND_-_GND@2, X010.pin1, D012.C, X011.pin1, J610.pin4, CP108.pin4, X100.pin1, J050.1, C010.0, C011.1, J051.1, J052.1, J452.1, J451.1, J053.1, J453.1, J032.1, J031.1
  131: Mega2560_Rev3.RESET, Q130.C, R130.Pin_1
  12V: Mega2560_Rev3.VIN, J420.2, J421.2, J591.1, R101.Pin_0, R651.Pin_0, SG655.1
  N1: J110.1, R111.Pin_1
  N2: J110.2, Q110.C
  N3: J120.1, R121.Pin_1
  N4: J120.2, Q120.C
  N5: Q130.B, R132.Pin_1
  N6: Q140.B, R142.Pin_0
  141: Q140.C, R140.Pin_1
  N7: Q120.B, R120.Pin_0
  N8: Q110.B, R110.Pin_0
  N9: IC100.GND, D102.A
  N10: IC100.IN, D100.cathode, C100.1
  5V: IC100.OUT, R111.Pin_0, R121.Pin_0, RH680.Vcc, R130.Pin_0, R140.Pin_0, J101.1, C101.1, J620.1, J622.1, J623.1, J626.1, J621.1, J540.1, J450.2, J591.2, J107.1, R680.Pin_0, J106.1, J624.1, J625.1, J610.pin1, CP108.pin1
  N11: D101.A, D102.C
  110: R110.Pin_1
  120: R120.Pin_1
  680: RH680.Data-signal, R680.Pin_1
  N12: D100.anode, X100.pin2
  106: J101.2
  N13: J101.3, R105.Pin_0
  105B: R142.Pin_1, J105.4
  105A: R132.Pin_0, J105.3
  N14: Q650.B, R650.Pin_1
  N15: Q650.C, J650.2
  N16: Q655.B, R655.Pin_1
  N17: Q655.C, SG655.2
  650: R650.Pin_0
  655: R655.Pin_0
  450A: J450.3
  450B: J450.4
  N18: J105.2, R121_2.Pin_1
  101: R101.Pin_1, R102.Pin_0
  121: R121_2.Pin_0
  105: R106.Pin_0, R105.Pin_1
  590A: J590.1, J590.2
  N19: DEV-10182.OUTA1, X031.pin2
  N20: DEV-10182.OUTB1, X031.pin1
  N21: DEV-10182.OUTA2, X032.pin2
  N22: DEV-10182.OUTB2, X032.pin1
  N23: DEV-10182.VCC, IC010.IN, ACS713.IP-, C010.1, D013.C
  050A: DEV-10182.CS1_-_A2, J050.3
  050B: DEV-10182.CS2_-_A3, J050.4
  052B: DEV-10182.INA2_-_D4, J052.3
  051A: DEV-10182.PWM1_-_D5, J051.2
  052A: DEV-10182.PWM2_-_D6, J052.2
  051C: DEV-10182.INA1_-_D7, J051.4
  051B: DEV-10182.INB1_-_D8, J051.3
  052C: DEV-10182.INB2_-_D9, J052.4
  010: X010.pin2, ACS713.IP+, J011.3
  N24: IC010.GND, D010.A
  N25: IC010.OUT, X011.pin2, C011.0, D013.A
  N26: ACS713.5V, J011.1
  N27: ACS713.VO, J011.2
  N28: ACS713.GND, J011.4
  N29: D010.C, D011.A
  N30: D011.C, D012.A
  610A: J610.pin2
  610B: J610.pin3
  108A: CP108.pin2
  108B: CP108.pin3
  N31: J650.1, R651.Pin_1
  N32: J050.2, J032.2, J031.2
  452A: J452.2
  452B: J452.3
  452C: J452.4
  451A: J451.2
  451B: J451.3
  451C: J451.4
  453A: J453.2
  453B: J453.3

notes:
  U-BoatMC, U-Boat Module Controll - Arduino Shields, 0.11
  GPS
  BTK
  TMP
  PRS
  RDT
  RDD
  AMB
  AMM
  AMC
  RPi
  HUB
  SNB
  SNF
  CLR
  CLL
  FLD
  CLB
  CLF
  BATTERY
  LED
  MTM
  MTB
  AMT
  5V
  GND
  MEnSnI
  BlTSnI
  MEnSpd
  MEnAhd
  MEnAst
  BlTEmr
  BlTDvn
  BlTSpd
  MEnTmp
  BlTTmp
  RdrDir
  7.2V
  RdrDpt
  FSH
  LNK
  CMPS10
