# Fritzing sketch UMC_AUX1310_0305 (saved by Fritzing 0.8.7b)
circuit board: 8cm x 8cm
breadboards: 1

parts:
  RH680 = Humidity and Temperature Sensor RHT03
  J620 = Header 3 [package=molex-1x3_lock]
  J622 = Header 3 [package=molex-1x3_lock]
  J623 = Header 3 [package=molex-1x3_lock]
  Q650 = TRANSISTOR_NPN [package=to-92]
  Q655 = TRANSISTOR_NPN [package=to-92]
  R650 = Resistor [tolerance=±5% resistance=1k package=THT]
  R655 = Resistor [tolerance=±5% resistance=1k package=THT]
  J621 = Header 3 [package=molex-1x3_lock]
  R680 = Resistor [tolerance=±5% resistance=1.5k package=THT]
  J624 = Header 3 [package=molex-1x3_lock]
  J625 = Header 3 [package=molex-1x3_lock]
  J601 = female pin header, 8 pins [form="♀ (female)"]
  J610 = female pin header, 4 pins [form="♀ (female)"]
  J600 = female pin header, 8 pins [form="♀ (female)"]
  R651 = Resistor [tolerance=±5% resistance=220 package=THT]
  SG655 = Buzzer 12mm [package=buzzer-12mm-ns-kit]
  J631 = female pin header, 4 pins [form="♀ (female)"]
  J630 = female pin header, 3 pins [form="♀ (female)"]
  J633 = female pin header, 3 pins [form="♀ (female)"]
  J651 = Header 2 [package=molex-1x2_lock]
  Q651 = TRANSISTOR_NPN [package=to-92]
  R652 = Resistor [tolerance=±5% resistance=1k package=THT]
  J632 = female pin header, 4 pins [form="♀ (female)"]
  J611 = female pin header, 6 pins [form="♀ (female)"]
  J626 = Header 3 [package=molex-1x3_lock]
  J627 = female pin header, 6 pins [form="♀ (female)"]
  J650 = Header 2 [package=molex-1x2_lock]

nets:
  5.4V: RH680.Vcc, J620.2, J622.2, J623.2, J621.2, R680.Pin_0, J624.2, J625.2, J630.pin2, J626.2, J627.pin2
  600D: RH680.Data-signal, R680.Pin_1, J600.pin1
  GND: RH680.GND_2, J620.1, J622.1, J623.1, Q650.E, Q655.E, J621.1, J624.1, J625.1, J630.pin1, J633.pin1, Q651.E, J626.1, J627.pin1
  602A: J620.3, J633.pin3
  N1: J622.3, J601.pin8
  N2: J623.3, J601.pin7
  N3: Q650.B, R650.Pin_1
  N4: Q650.C, J650.2
  N5: Q655.B, R655.Pin_1
  N6: Q655.C, SG655.2
  600B: R650.Pin_0, J600.pin4
  600A: R655.Pin_0, J600.pin5
  602B: J621.3, J633.pin2
  N7: J624.3, J601.pin6
  N8: J625.3, J601.pin5
  N9: J601.pin1, J627.pin6
  N10: J601.pin2, J627.pin5
  N11: J601.pin3, J627.pin4
  N12: J601.pin4, J626.3
  N13: J610.pin1, J631.pin1
  N14: J610.pin2, J631.pin2
  N15: J610.pin3, J631.pin4
  N16: J610.pin4, J631.pin3
  N17: J600.pin2, J627.pin3
  600C: J600.pin3, R652.Pin_0
  7.2V: R651.Pin_0, SG655.1, J630.pin3, J651.1
  N18: R651.Pin_1, J650.1
  N19: J651.2, Q651.C
  N20: Q651.B, R652.Pin_1
  N21: J632.pin1, J611.pin6
  N22: J632.pin2, J611.pin1
  N23: J632.pin3, J611.pin2
  N24: J632.pin4, J611.pin3

notes:
  SNB
  SNF
  CSN
  FLD
  CPT
  CSD
  LGT
  U-BoatMC, U-Boat Module Controll - Auxiliary Shields, 0.305
  GND
  SonarF
  5V
  CBW
  CllSrW
  CllSrN
  CllSrT
  CllSrD
  FloodS
  K
  A
  SonarB
  AuxLgt
  Buzzer
  DHTSns
  37 35 33 31 29 27 25 23
  53 51 49 47 45 43 41 39
  N.C.
  SgHorn
  CllSrR
  CllSrL
  CllSrB
  CllSrF
  IOAux4
  IOAux2
  IOAux3
  IOAux1
  SNR
  AUX
  RX
  CMPS10
  TX
  GPS
  5.4V
  7.2V
  RDD
  HRN
  CMP
  SDA
  SCL
  EM406
  M
  +
  UMC_AUX1310 V0.305
