# Fritzing sketch UMC_PWR1310_0305 (saved by Fritzing 0.8.7b)
circuit board: 10.1776cm x 5.36194cm
breadboards: 1

parts:
  IC010 = Voltage Regulator [part_number=uA7805 package=to-220-alt]
  D010 = Diode [part_number=1N4148 package=diode-1n4148]
  D011 = Diode [part_number=1N4148 package=diode-1n4148]
  D012 = Diode [part_number=1N4148 package=diode-1n4148]
  C010 = Ceramic Capacitor [capacitance=100nF package="100 mil [THT, multilayer]"]
  C011 = Ceramic Capacitor [capacitance=100nF package="100 mil [THT, multilayer]"]
  D014 = Diode [part_number=1N4007 package=diode-1n4148]
  J053 = Header 4 [package=molex-1x4_lock]
  J052 = Header 4 [package=molex-1x4_lock]
  J051 = Header 3 [package=molex-1x3_lock]
  J032 = Header 3 [package=molex-1x3_lock]
  J031 = Header 3 [package=molex-1x3_lock]
  J050 = Header 3 [package=molex-1x3_lock]
  DEV-10182 = Monster Moto Shield
  ACS712 = ACS712 Low Current Sensor Board v12
  J061 = Header 3 [package=molex-1x3_lock]
  J010 = Header 4 [package=jst-4-pth]
  J011 = Header 3 [package=jst-3-pth]
  J060 = Header 3 [package=molex-1x3_lock]
  X010 = screw terminal, 2 pins
  X031 = screw terminal, 2 pins
  X032 = screw terminal, 2 pins
  X011 = screw terminal, 2 pins
  D013 = Diode [part_number=1N4148 package=diode-1n4148]

nets:
  N1: IC010.GND, D010.A
  N2: IC010.IN, C010.1, D014.C, DEV-10182.VCC, ACS712.IP-
  7.2V: IC010.OUT, C011.0, D014.A, J061.2, J060.2, X011.pin2
  N3: D010.C, D011.A
  N4: D011.C, D012.A
  N5: D012.C, D013.A
  GND: C010.0, C011.1, J053.1, J052.1, J051.1, J032.1, J031.1, J050.1, DEV-10182.GND, DEV-10182.GND_-_GND@0, DEV-10182.GND_-_GND@1, DEV-10182.GND_-_GND@2, ACS712.GND, J061.1, J010.1, J011.1, J060.1, X010.pin1, X011.pin1, D013.C
  051A: J053.2, DEV-10182.PWM1_-_D5
  051B: J053.3, DEV-10182.INA1_-_D7
  051C: J053.4, DEV-10182.INB1_-_D8
  052A: J052.2, DEV-10182.PWM2_-_D6
  052B: J052.3, DEV-10182.INA2_-_D4
  052C: J052.4, DEV-10182.INB2_-_D9
  N6: J051.2, J031.3
  N7: J051.3, J032.3
  5.4V: J032.2, J031.2, DEV-10182.5V, ACS712.5V, J010.2
  050A: J050.2, DEV-10182.CS1_-_A2
  050B: J050.3, DEV-10182.CS2_-_A3
  N8: DEV-10182.OUTA1, X031.pin1
  N9: DEV-10182.OUTB1, X031.pin2
  N10: DEV-10182.OUTA2, X032.pin1
  N11: DEV-10182.OUTB2, X032.pin2
  010: ACS712.IP+, J010.4, X010.pin2
  N12: ACS712.VO, J010.3
  N13: J061.3, J011.3
  N14: J011.2, J060.3

notes:
  BATTERY
  AME
  AMB
  AMC
  MTB
  MTE
  AMT
  MEnSnI
  BlTSnI
  GND
  MEnAhd
  MEnAst
  MEnSpd
  BlTDvn
  BlTEmr
  BlTSpd
  BlTTmp
  MEnTmp
  AMS
  EngBtV
  5.4V
  EngBtI
  AMP
  7.2V
  U-BoatMC, U-Boat Module Controll - Power Shields, 0.305
  PWR
  +
  -
  SNR
  Current Sense
  RDT
  RDD
  RdrDpt
  RdrDir
  AMR
  M
  UMC_PWR1310 V0.305
